# Fritzing sketch SmartKanne_0.1 (saved by Fritzing 0.9.3b)
breadboards: 1

parts:
  Onderdeel1 = Arduino Uno (Rev3)
  LCD1 = LCD screen
  J1 = Piezo Speaker
  R1 = Resistor [tolerance=±5% resistance=220 package=THT]
  DS1 = DS18B20 1-Wire Temperature Sensor [part_number=DS18B20]
  R2 = Resistor [tolerance=±5% resistance=4.7k package=THT]
  S1 = Momentary Switch [package=ksa_sealed_tac_switch]
  LCM1602_IIC2 = LCM1602 IIC [part_number="LCM1602 IIC" chip_label="LCM1602 IIC" package="DIP (Dual Inline) [THT]"]
  Part1 = RFID-RC522-v2
  S2 = Momentary Switch [package=ksa_sealed_tac_switch]
  VCC1 = Battery
  VCC3 = Battery
  VCC4 = Battery  # not connected

nets:
  N1: Onderdeel1.A5/SCL, LCM1602_IIC2.SCL
  N2: Onderdeel1.D9_PWM, Part1.RST
  N3: Onderdeel1.D10_PWM/SS, Part1.SDA
  N4: Onderdeel1.D11_PWM/MOSI, Part1.MOSI
  N5: Onderdeel1.D12/MISO, Part1.MISO
  N6: Onderdeel1.D13/SCK, Part1.SCK
  N7: Onderdeel1.A4/SDA, LCM1602_IIC2.SDA
  N8: Onderdeel1.D2, DS1.DQ, R2.Pin_0
  N9: Onderdeel1.D3_PWM, S2.3, S2.4
  N10: Onderdeel1.D4, S1.3, S1.4
  N11: Onderdeel1.D7, R1.Pin_0
  3V3: Onderdeel1.3V3, Part1.3.3V
  5V: Onderdeel1.5V, DS1.VDD, R2.Pin_1, LCM1602_IIC2.VCC
  GND: Onderdeel1.GND, J1.pin1, DS1.GND, S1.1, S1.2, LCM1602_IIC2.GND, Part1.GND, S2.1, S2.2, VCC3.-
  N12: Onderdeel1.VIN, VCC1.+
  VSS: LCD1.VSS, LCM1602_IIC2.VSS
  VDD: LCD1.VDD, LCM1602_IIC2.VDD
  N13: LCD1.V0, LCM1602_IIC2.V0
  N14: LCD1.RS, LCM1602_IIC2.RS
  N15: LCD1.R/W, LCM1602_IIC2.RW
  N16: LCD1.E, LCM1602_IIC2.E
  N17: LCD1.DB0, LCM1602_IIC2.D0
  N18: LCD1.DB1, LCM1602_IIC2.D1
  N19: LCD1.DB2, LCM1602_IIC2.D2
  N20: LCD1.DB3, LCM1602_IIC2.D3
  N21: LCD1.DB4, LCM1602_IIC2.D4
  N22: LCD1.DB5, LCM1602_IIC2.D5
  N23: LCD1.DB6, LCM1602_IIC2.D6
  N24: LCD1.DB7, LCM1602_IIC2.D7
  N25: LCD1.LED+, LCM1602_IIC2.A
  N26: LCD1.LED-, LCM1602_IIC2.K
  N27: J1.pin2, R1.Pin_1
  N28: LCM1602_IIC2.LED_A, LCM1602_IIC2.LED_B

custom parts:
  LCM1602 IIC: I2C-Module to use a 1602 or 2004 LCD on with the wire.h libory Serial LCD Modul
  RFID-RC522-v2: A simple China made RFID-RC522 Reader; do check the pin labels, as this is a MFRC522 based clone.
